# Fritzing sketch rgb_led_pwm_decade_counter (saved by Fritzing 0.5.2b)
breadboards: 1

parts:
  Arduino1 = Arduino
  IC1 = IC, DIP package, 16 pins [chip_label="MC14017B Decade Counter" spacing=300mil]
  Q1 = NPN-Transistor [package="TO92 [THT]"]
  Q2 = NPN-Transistor [package="TO92 [THT]"]
  Q3 = NPN-Transistor [package="TO92 [THT]"]
  Q4 = NPN-Transistor [package="TO92 [THT]"]
  LED5 = RGB LED - (4 legs)
  LED6 = RGB LED - (4 legs)
  LED7 = RGB LED - (4 legs)
  LED4 = RGB LED - (4 legs)
  R1 = Resistor [resistance=2.2k package=THT]
  R2 = Resistor [resistance=2.2k package=THT]
  R3 = Resistor [resistance=2.2k package=THT]
  R4 = Resistor [resistance=2.2k package=THT]
  R5 = Resistor [resistance=470 package=THT]
  R6 = Resistor [resistance=470 package=THT]
  R7 = Resistor [resistance=470 package=THT]

nets:
  N1: Arduino1.D9, R7.Pin_1
  N2: Arduino1.D5, R6.Pin_1
  N3: Arduino1.D4, IC1.pin15
  N4: Arduino1.D3, R5.Pin_1
  N5: Arduino1.D2, IC1.pin14
  N6: Arduino1.+5V, IC1.pin16
  N7: Arduino1.GND, IC1.pin8, IC1.pin13, Q1.E, Q2.E, Q3.E, Q4.E
  N8: IC1.pin2, R1.Pin_1
  N9: IC1.pin4, R2.Pin_1
  N10: IC1.pin7, R3.Pin_1
  N11: IC1.pin10, R4.Pin_1
  N12: Q1.B, R4.Pin_0
  N13: Q1.C, LED7.connector1
  N14: Q2.B, R3.Pin_0
  N15: Q2.C, LED6.connector1
  N16: Q3.B, R2.Pin_0
  N17: Q3.C, LED5.connector1
  N18: Q4.B, R1.Pin_0
  N19: Q4.C, LED4.connector1
  N20: LED5.connector2, LED6.connector2, LED7.connector2, LED4.connector2, R6.Pin_0
  N21: LED5.connector3, LED6.connector3, LED7.connector3, LED4.connector3, R7.Pin_0
  N22: LED7.connector0, LED4.connector0, R5.Pin_0
